# Fritzing sketch perfboard-design (saved by Fritzing 0.9.4)
perfboards: 3

parts:
  Pololu_A1 = Pololu A4988 [package=SO16]  # not connected
  Pololu_A2 = Pololu A4988 [package=SO16]  # not connected
  Pololu_A3 = Pololu A4988 [package=SO16]  # not connected
  Pololu_A4 = Pololu A4988 [package=SO16]  # not connected
  Pololu_A5 = Pololu A4988 [package=SO16]  # not connected
  Pololu_A6 = Pololu A4988 [package=SO16]  # not connected
  J1 = Camdenboss CTB0158-2 [part_number=CTB0158-2 package=THT]  # not connected
  J2 = male pin header, 4 pins [form="♂ (male)"]  # not connected
  J3 = male pin header, 4 pins [form="♂ (male)"]  # not connected
  J4 = male pin header, 4 pins [form="♂ (male)"]  # not connected
  J5 = male pin header, 4 pins [form="♂ (male)"]  # not connected
  J6 = male pin header, 4 pins [form="♂ (male)"]  # not connected
  J7 = male pin header, 4 pins [form="♂ (male)"]  # not connected
  Raspberry_Pi_1 = Raspberry Pi 3 [part_number=RPI-3-V1.2]
  C1 = Electrolytic Capacitor [capacitance=100µF voltage=50V package="100 mil [THT, electrolytic]"]  # not connected
  C2 = Electrolytic Capacitor [capacitance=100µF voltage=50V package="100 mil [THT, electrolytic]"]  # not connected
  C3 = Electrolytic Capacitor [capacitance=100µF voltage=50V package="100 mil [THT, electrolytic]"]  # not connected
  C4 = Electrolytic Capacitor [capacitance=100µF voltage=50V package="100 mil [THT, electrolytic]"]  # not connected
  C5 = Electrolytic Capacitor [capacitance=100µF voltage=50V package="100 mil [THT, electrolytic]"]  # not connected
  C6 = Electrolytic Capacitor [capacitance=100µF voltage=50V package="100 mil [THT, electrolytic]"]  # not connected
  Pololu_A7 = Pololu A4988 [package=SO16]  # not connected
  Pololu_A8 = Pololu A4988 [package=SO16]  # not connected
  Pololu_A9 = Pololu A4988 [package=SO16]  # not connected
  J8 = Camdenboss CTB0158-2 [part_number=CTB0158-2 package=THT]  # not connected
  C7 = Electrolytic Capacitor [capacitance=100µF voltage=50V package="100 mil [THT, electrolytic]"]  # not connected
  C8 = Electrolytic Capacitor [capacitance=100µF voltage=50V package="100 mil [THT, electrolytic]"]  # not connected
  C9 = Electrolytic Capacitor [capacitance=100µF voltage=50V package="100 mil [THT, electrolytic]"]  # not connected
  Step = female pin header, 6 pins [form="♀ (female)"]  # not connected

nets:
  N1: Raspberry_Pi_1.GPIO14, Raspberry_Pi_1.GND
